# Fritzing sketch Maletin Impreso V3 (saved by Fritzing 0.9.3b)
circuit board: 5cm x 6cm
breadboards: 1

parts:
  part = Adafruit Metro Mini [part_number="Adafruit #2590"]
  part_2 = NRF24L01+ Breakout Board
  part_3 = Lithium Ion Polymer Battery 3.7v 150mAh [part_number=1317]
  D1 = Header 1 [package=1x01_offset]
  -1 = Header 1 [package=1x01_offset]
  +1 = Header 1 [package=1x01_offset]
  D2 = Header 1 [package=1x01_offset]
  -2 = Header 1 [package=1x01_offset]
  +2 = Header 1 [package=1x01_offset]
  D3 = Header 1 [package=1x01_offset]
  -3 = Header 1 [package=1x01_offset]
  +3 = Header 1 [package=1x01_offset]
  D4 = Header 1 [package=1x01_offset]
  -4 = Header 1 [package=1x01_offset]
  +4 = Header 1 [package=1x01_offset]
  BLE = Bluetooth HC-05 Macho

nets:
  N1: part.IO13, part_2.SCK
  N2: part.IO12, part_2.MISO
  N3: part.IO11, part_2.MOSI
  N4: part.IO10, part_2.CS
  N5: part.IO9, part_2.CE
  N6: part.IO8, D1.1
  N7: part.IO7, D2.1
  N8: part.IO6, D3.1
  N9: part.IO5, D4.1
  N10: part.IO1, BLE.RXD
  N11: part.IO0, BLE.TXD
  VCC: part.3.3V, part_2.VCC, +1.1, +2.1, +3.1, +4.1, BLE.VCC
  GND: part.GND, part_2.GND, part_3.negative, -1.1, -2.1, -3.1, -4.1, BLE.GND
  N12: part.VIN, part_3.positive

custom parts:
  Adafruit Metro Mini: We sure love the ATmega328 here at Adafruit, and we use them a lot for our own projects. The processor has plenty of GPIO, Analog inputs, hardware UART SPI and I2C, timers and PWM galore - just enough for most simple projects. When we need to go small, we use a Pro Trinket 3V or 5V, but if you want to have USB-to-Serial built in, we reach for an Adafruit METRO Mini. METRO Mini is the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
  Lithium Ion Polymer Battery 3.7v 150mAh: Lithium ion polymer (also known as 'lipo' or 'lipoly') batteries are thin, light and powerful. The output ranges from 4.2V when completely charged to 3.7V. This battery has a capacity of 150mAh for a total of about 0.6 Wh. The batteries come pre-attached with a genuine 2-pin JST-PH connector as shown and include the necessary protection circuitry.
